# Fritzing sketch Power Water (saved by Fritzing 0.9.3b)
circuit board: 3.65601cm x 2.62053cm
breadboards: 1

parts:
  Power_plug1 = Power plug
  IC1 = Voltage Regulator [package=to220-igo]
  JP1 = Header 1 [package=1x01_offset]
  JP2 = Header 1 [package=1x01_offset]
  JP3 = Header 1 [package=1x01_offset]
  J1_Pump = screw terminal, 4 pins
  C1 = Electrolytic Capacitor [capacitance=10μF package="100 mil [THT, electrolytic]"]
  C2 = Electrolytic Capacitor [capacitance=10μF package="100 mil [THT, electrolytic]"]
  U3 = HK4100F RELAY [package=relay-shg]

nets:
  GND: Power_plug1.GND, IC1.GND, JP2.1, J1_Pump.pin2, J1_Pump.pin4, C1.-, C2.-, U3.4
  N1: Power_plug1.VCC, IC1.IN, C1.+, U3.5, U3.6
  N2: IC1.OUT, JP1.1, C2.+
  N3: JP3.1, U3.3
  N4: J1_Pump.pin1, J1_Pump.pin3, U3.1

notes:
  12V rail
  5V rail

custom parts:
  HK4100F RELAY: SPDT relay (HK4100F)
