# Fritzing sketch mainboard (saved by Fritzing 0.9.3b)
circuit board: 8.2cm x 5.8cm
breadboards: 2

parts:
  U1 = atmega328 [package=dip]
  XTAL1 = Crystal [frequency="16 Mhz" package=THT]
  C1 = Ceramic Capacitor [capacitance=22pF package="100 mil [THT, multilayer]"]
  C2 = Ceramic Capacitor [capacitance=22pF package="100 mil [THT, multilayer]"]
  R1 = Resistor [tolerance=±5% resistance=10k package=THT]
  12V = 2.1mm DC Barrel Jack
  ICSP = double row male pin header, 6 pins [form="♂ (male)"]
  Lamp_Relay = OMRON PCB Power Relay – G5LE [part_number="G5LE-1\n" package=THT]
  RTC_&_SD = male pin header, 8 pins [form="♂ (male)"]
  TX = male pin header, 1 pin [form="♂ (male)"]
  Flow_Sensor = male pin header, 3 pins [form="♂ (male)"]
  MHUM = male pin header, 4 pins [form="♂ (male)"]
  UI_Panel = male pin header, 9 pins [form="♂ (male)"]
  C4 = Electrolytic Capacitor [capacitance=10µF voltage=20V package="100 mil [THT, electrolytic]"]
  C3 = Electrolytic Capacitor [capacitance=10µF voltage=20V package="100 mil [THT, electrolytic]"]
  Pump_Relay = HK4100F RELAY [package=relay-shg]
  Lamp = Screw terminal - 2 pins [package=THT]
  Buoy = male pin header, 2 pins [form="♂ (male)"]
  Pump = male pin header, 2 pins [form="♂ (male)"]
  IC2 = Voltage Regulator [package=78xxl]

nets:
  N1: U1.RESET, R1.Pin_0, ICSP.pin3
  N2: U1.D0_(RX), Lamp_Relay.COIL2
  N3: U1.D1_(TX), TX.pin1
  N4: U1.D2, Flow_Sensor.pin3
  N5: U1.D3_(PWM), UI_Panel.pin6
  N6: U1.D4, UI_Panel.pin8
  N7: U1.VCC, U1.AVCC, R1.Pin_1, ICSP.pin6, RTC_&_SD.pin5, Flow_Sensor.pin2, MHUM.pin1, UI_Panel.pin2, C4.+, IC2.OUT
  GND: U1.GND, C1.1, C2.1, 12V.switch, ICSP.pin4, Lamp_Relay.COIL1, RTC_&_SD.pin6, Flow_Sensor.pin1, MHUM.pin2, UI_Panel.pin3, C4.-, C3.-, Pump_Relay.3, Buoy.pin2, Pump.pin2, IC2.GND
  N8: U1.XLAT1, XTAL1.pin_0, C1.0
  N9: U1.XLAT2, XTAL1.pin_1, C2.0
  N10: U1.D5_(PWM), UI_Panel.pin9
  N11: U1.D6_(PWM), UI_Panel.pin7
  N12: U1.D7, UI_Panel.pin1
  N13: U1.D8, UI_Panel.pin5
  N14: U1.D9_(PWM), Pump_Relay.4
  N15: U1.D10_(PWM), RTC_&_SD.pin1
  N16: U1.D11_(PWM), ICSP.pin5, RTC_&_SD.pin2
  N17: U1.D12, ICSP.pin1, RTC_&_SD.pin3
  N18: U1.D13, ICSP.pin2, RTC_&_SD.pin4
  N19: U1.A0, MHUM.pin3
  N20: U1.A1, MHUM.pin4
  N21: U1.A2, UI_Panel.pin4
  N22: U1.A3, Buoy.pin1
  N23: U1.A4, RTC_&_SD.pin7
  N24: U1.A5, RTC_&_SD.pin8
  N25: 12V.center, C3.+, Pump_Relay.5, Pump_Relay.6, IC2.IN
  N26: Lamp_Relay.A, Lamp.pin2
  N27: Lamp_Relay.C, Lamp.pin1
  N28: Pump_Relay.1, Pump.pin1

notes:
  12V
  5V
  VCC MOSI GND
  MISO SCK RST
  buz pwr gnd but clk dsr Vo en rs
  GND PWR PD2
  PWR GND SM SH
  SDCS MOSI MISO SCLK PWR GND SDA SCL

custom parts:
  2.1mm DC Barrel Jack: 2.1mm DC Barrel Jack with Thru-Hole Connectors (breadboardable)
  HK4100F RELAY: SPDT relay (HK4100F)
