# Fritzing sketch ui-panel (saved by Fritzing 0.9.3b)
circuit board: 6.22215cm x 4.63363cm
breadboards: 1

parts:
  S2 = Momentary Switch [package=ksa_sealed_tac_switch]
  S3 = Momentary Switch [package=ksa_sealed_tac_switch]
  S4 = Momentary Switch [package=ksa_sealed_tac_switch]
  R2 = Resistor [tolerance=±5% resistance=1.8k package=THT]
  R1 = Resistor [tolerance=±5% resistance=1.8k package=THT]
  R3 = Resistor [tolerance=±5% resistance=1.8k package=THT]
  R4 = Resistor [tolerance=±5% resistance=16k package=THT]
  R5 = TRIMPOT [package=trimpot_pth_s3_lock]
  U1 = CD54HC194 [package="DIP16 [THT]"]
  R6 = Resistor [tolerance=±5% resistance=560 package=THT]
  J6 = female pin header, 1 pin [form="♀ (female)"]
  J5 = female pin header, 1 pin [form="♀ (female)"]
  J14 = female pin header, 7 pins [form="♀ (female)"]
  J13 = female pin header, 10 pins [form="♀ (female)"]
  LCD1 = LCD screen
  S5 = Toggle Switch [package=THT]
  SG1 = Buzzer 12mm [package=buzzer-12mm-ns]
  S1 = Momentary Switch [package=ksa_sealed_tac_switch]
  C1 = Ceramic Capacitor [capacitance=100nF package="100 mil [THT, multilayer]"]

nets:
  N1: S2.2, S3.2, S4.2, J14.pin3, S1.2
  N2: S2.4, R2.Pin_0, R1.Pin_1
  N3: S3.4, R2.Pin_1, R3.Pin_0
  net label: S4.4, R3.Pin_1
  GND: R1.Pin_0, R4.Pin_0, R5.CW, U1.GND, U1.S1, J14.pin2, J13.pin1, J13.pin4, J13.pin6, LCD1.VSS, LCD1.R/W, LCD1.LED-, S1.4, C1.1
  N4: R4.Pin_1, J6.pin1, SG1.1
  VCC: R5.CCW, U1.MR, U1.S0, U1.VCC, J14.pin1, J13.pin2, LCD1.VDD, C1.0
  N5: R5.WIPER, J13.pin3, LCD1.V0
  N6: U1.DSR, J14.pin5
  N7: U1.CP, J14.pin4
  N8: U1.Q3, J13.pin7, LCD1.DB7
  N9: U1.Q2, J13.pin8, LCD1.DB6
  N10: U1.Q1, J13.pin9, LCD1.DB5
  N11: U1.Q0, J13.pin10, LCD1.DB4
  N12: R6.Pin_0, J14.pin6
  N13: R6.Pin_1, J13.pin5, LCD1.LED+
  N14: J5.pin1, J14.pin7, S5.COM, SG1.2

notes:
  PD3: DSR
  PC0: buttons
  PB0: CLK
  GND in
  PWR in
  LCD Pins
  LCD Power
  PC3: LCD Vo
  Buzzer Switch
  1
  D4 D5 D6  D7 GND Vee GND Vo PWR GND

custom parts:
  CD54HC194: 4-Bit Bidirectional Universal Shift Register
